// Logisim project TinyCPU-AddressPath.circ as structural Verilog: 1 circuit, main circuit AddressPath
module AddressPath (
  input  [11:0] ADDRESS_IN,
  input  [11:0] OFFSET,
  input  AR_LOAD,
  input  VALID_IN,
  input  CLK,
  output [11:0] ADDRESS,
  output ADDRESS_VALID,
  output [11:0] ADDRESS_PLUS_OFFSET,
  output OFFSET_CARRY
);

  Register #(.width(12)) AR (.D(ADDRESS_IN), .Q(OFFSET), .clk(AR_LOAD));  // open: en, clr
  // Register #(.width(1)) AR_VALID: pin names not known; wires that end beside it: VALID_IN, ADDRESS_VALID, OFFSET
  // Adder #(.width(12)) OFFSET_ADDER: pin names not known; wires that end beside it: OFFSET, ADDRESS_PLUS_OFFSET, OFFSET_CARRY

  assign ADDRESS = OFFSET;

  // Notes on the sheet:
  //   Clocked 12-bit address register with combinational offset addition
endmodule
