// Logisim project TinyCPU-FetchDecode.circ as structural Verilog: 1 circuit, main circuit FetchDecode
module FetchDecode (
  input  CLK,
  input  RESET,
  input  ZERO,
  input  [11:0] PROGRAM_LIMIT,
  input  NEGATIVE,
  input  ERROR,
  output [15:0] OPERAND,
  output LOAD_CONST,
  output STORE_ADDRESS,
  output ADD_ADDRESS,
  output JUMP_NOT_ZERO,
  output PRINT,
  output HALT,
  output SET_ADDR,
  output HALT_ERROR,
  output [11:0] PC_OUT,
  output LOAD_ADDRESS,
  output LOAD_ADDRESS_REGISTER,
  output LOAD_ADDRESS_REGISTER_PLUS_OFFSET,
  output ADD_CONST,
  output ADD_ADDRESS_REGISTER,
  output ADD_ADDRESS_REGISTER_PLUS_OFFSET,
  output SUB_CONST,
  output SUB_ADDRESS,
  output SUB_ADDRESS_REGISTER,
  output SUB_ADDRESS_REGISTER_PLUS_OFFSET,
  output MUL_CONST,
  output MUL_ADDRESS,
  output MUL_ADDRESS_REGISTER,
  output MUL_ADDRESS_REGISTER_PLUS_OFFSET,
  output DIV_CONST,
  output DIV_ADDRESS,
  output DIV_ADDRESS_REGISTER,
  output DIV_ADDRESS_REGISTER_PLUS_OFFSET,
  output AND_CONST,
  output AND_ADDRESS,
  output AND_ADDRESS_REGISTER,
  output AND_ADDRESS_REGISTER_PLUS_OFFSET,
  output OR_CONST,
  output OR_ADDRESS,
  output OR_ADDRESS_REGISTER,
  output OR_ADDRESS_REGISTER_PLUS_OFFSET,
  output STORE_ADDRESS_REGISTER,
  output STORE_ADDRESS_REGISTER_PLUS_OFFSET,
  output LOAD_ADDRESS_REGISTER_CONST,
  output LOAD_ADDRESS_REGISTER_ADDRESS,
  output NOT,
  output JUMP_ADDRESS,
  output JUMP_ZERO,
  output JUMP_NEGATIVE,
  output JUMP_ERROR,
  output JUMP_NOT_ERROR,
  output CLEAR_ERROR,
  output INPUT,
  output PRINT_ADDRESS,
  output SET_OVF,
  output SET_DIV0,
  output SET_INV,
  output SET_ILL,
  output SET_INPUT
);

  wire [10:5] PC_INCREMENT_p1;

  Register #(.width(12)) PC ();  // open: D, en, clk, Q, clr
  // Adder #(.width(12)) PC_INCREMENT: pin names not known; wires that end beside it: {PC_INCREMENT_p1, OPERAND[15:12], PROGRAM_LIMIT[11:1], CLK}, {PC_INCREMENT_p1, OPERAND[15:12], PROGRAM_LIMIT[11:1], CLK}
  Multiplexer #(.select(1), .width(12)) PC_SOURCE (.out({PROGRAM_LIMIT[11:1], CLK}));  // open: in0, in1, sel
  ROM #(.addrWidth(12), .dataWidth(22)) INSTRUCTION_ROM (
    .addr({PROGRAM_LIMIT[11:1], CLK}), .data({PC_INCREMENT_p1, OPERAND[15:12], PROGRAM_LIMIT[11:1], CLK}));
  Comparator #(.width(12)) PC_RANGE (
    .a({PROGRAM_LIMIT[11:1], CLK}), .b({PROGRAM_LIMIT[11:1], CLK}), .eq(CLK));  // open: gt, lt
  // Decoder #(.select(6)) ISA_DECODER: pin names not known; wires that end beside it: {PC_INCREMENT_p1, OPERAND[15:12], PROGRAM_LIMIT[11:1], CLK}
  // AND_Gate JNZ_TAKEN has open pins: out=CLK
  // OR_Gate ERROR_HALT has open pins: out=CLK
  // Pins of 1 and 12 and 16 and 22 bits meet at {PC_INCREMENT_p1, OPERAND[15:12], PROGRAM_LIMIT[11:1], CLK}

  assign ADD_ADDRESS = CLK;
  assign HALT = CLK;
  assign HALT_ERROR = CLK;
  assign JUMP_NOT_ZERO = CLK;
  assign LOAD_CONST = CLK;
  assign OPERAND[11:0] = {PROGRAM_LIMIT[11:1], CLK};
  assign PC_OUT = {PROGRAM_LIMIT[11:1], CLK};
  assign PRINT = CLK;
  assign PROGRAM_LIMIT[0] = CLK;
  assign RESET = CLK;
  assign SET_ADDR = CLK;
  assign STORE_ADDRESS = CLK;

  // Notes on the sheet:
  //   AP 7 machine format v1: stable six-bit opcode allocation and encoder-generated ROM
  //   contents of INSTRUCTION_ROM (hex, n*v repeats v):
  //   00ffff 1c0065 000003 1c0064 2a0000 050065 1c0064 240004 2c0000
endmodule
